// Logisim project main.circ as structural Verilog: 9 circuits, main circuit main
module main (
  input  in_1
);

  wire ALUSrc, clk, EXTControl, MemRead, MemWrite, RegDst, RegWrite, Zero;
  wire [1:0] Mem2Reg, NPCControl;
  wire [2:0] ALUControl;
  wire [4:0] RegAddr, shamt, splitter_1_rd, splitter_1_rs, splitter_1_rt;
  wire [5:0] splitter_1_funct, splitter_1_opcode;
  wire [15:0] splitter_1_imm16;
  wire [25:0] splitter_1_imm26;
  wire [31:0] alu_1_aluout, beqImm32, dm_1_out_7, grf_1_out_8, ifu_1_pc, Instr, MemData, multiplexer_3_out,
       npc_1_out_7, RegData;

  Clock clock_1 (.out(clk));
  NPC npc_1 (
    .in_4(ifu_1_pc), .in_5(splitter_1_imm26), .Imm32(beqImm32), .reset(in_1), .NPCControl(NPCControl),
    .Zero(Zero), .out_7(npc_1_out_7));
  IFU ifu_1 (.out_4(Instr), .clk(clk), .reset(in_1), .NPC(npc_1_out_7), .PC(ifu_1_pc));
  Splitter splitter_1 (
    .Instr(Instr), .opcode(splitter_1_opcode), .rs(splitter_1_rs), .rt(splitter_1_rt), .rd(splitter_1_rd),
    .shamt(shamt), .funct(splitter_1_funct), .Imm26(splitter_1_imm26), .Imm16(splitter_1_imm16));
  Multiplexer #(.width(5)) multiplexer_1 (
    .in0(splitter_1_rt), .in1(splitter_1_rd), .out(RegAddr), .sel(RegDst));  // open: en
  Multiplexer #(.select(2), .width(32)) multiplexer_2 (
    .in0(alu_1_aluout), .in1(dm_1_out_7), .in2(MemData), .out(RegData), .sel(Mem2Reg));  // open: in3, en
  Controller controller_1 (
    .opcode(splitter_1_opcode), .funct(splitter_1_funct), .ALUControl(ALUControl), .MemRead(MemRead),
    .MemWrite(MemWrite), .RegWrite(RegWrite), .Mem2Reg(Mem2Reg), .EXTControl(EXTControl), .ALUSrc(ALUSrc),
    .RegDst(RegDst), .NPCControl(NPCControl));
  GRF grf_1 (
    .in_4(splitter_1_rs), .in_5(splitter_1_rt), .in_6(RegAddr), .in_7(RegData), .out_8(grf_1_out_8),
    .out_9(MemData), .in_1(clk), .in_2(in_1), .in_3(RegWrite));
  Multiplexer #(.width(32)) multiplexer_3 (
    .in0(MemData), .in1(beqImm32), .out(multiplexer_3_out), .sel(ALUSrc));  // open: en
  EXT ext_1 (.in_2(splitter_1_imm16), .out_3(beqImm32), .EXTControl(EXTControl));
  ALU alu_1 (
    .in_2(grf_1_out_8), .in_3(multiplexer_3_out), .ALUOut(alu_1_aluout), .Zero(Zero), .in_1(ALUControl),
    .in_4(shamt));
  DM dm_1 (.WD(MemData), .out_7(dm_1_out_7), .in_1(clk), .in_2(in_1), .in_3(MemWrite), .in_4(MemRead));  // open: A

  // Other names for the same wires on the sheet: reset = in_1
endmodule

module NPC (
  input  reset,
  input  [1:0] NPCControl,
  input  Zero,
  input  [31:0] in_4,
  input  [25:0] in_5,
  input  [31:0] Imm32,
  output [31:0] out_7
);

  wire [0:0] and_1_out;
  wire [3:0] bit_extender_2_out;
  wire [15:0] IMM16;
  wire [27:0] bit_extender_1_out, shifter_3_out;
  wire [31:0] adder_1_out, adder_2_out, shifter_1_out, shifter_2_out;

  assign bit_extender_1_out = {{2{1'b0}}, in_5};  // Bit_Extender bit_extender_1
  Adder #(.width(32)) adder_1 (.a(in_4), .b(32'h4), .out(adder_1_out));  // open: cin, cout
  Shifter #(.width(32)) shifter_1 (.in(Imm32), .\dist (5'b00010), .out(shifter_1_out));
  Bit_Extender #(.in_width(32), .out_width(4)) bit_extender_2 (.in(shifter_2_out), .out(bit_extender_2_out));
  Shifter #(.width(32), .shift("ar")) shifter_2 (.in(in_4), .\dist (5'b11100), .out(shifter_2_out));
  Shifter #(.width(28)) shifter_3 (.in(bit_extender_1_out), .\dist (5'b00010), .out(shifter_3_out));
  and and_1 (and_1_out[0], NPCControl[0], Zero);
  Bit_Extender #(.in_width(26)) bit_extender_3 (.in(in_5), .out(IMM16));
  Adder #(.width(32)) adder_2 (.a(adder_1_out), .b(shifter_1_out), .out(adder_2_out));  // open: cin, cout
  Multiplexer #(.select(2), .width(32)) multiplexer_1 (
    .in0(adder_1_out), .in1(adder_2_out), .in2({bit_extender_2_out, shifter_3_out}), .out(out_7),
    .sel({NPCControl[1], and_1_out[0]}));  // open: in3, en

  // Other names for the same wires on the sheet: IMM26[25:0] = in_5; PC[31:0] = in_4
endmodule

module IFU (
  input  clk,
  input  reset,
  input  [31:0] NPC,
  output [31:0] out_4,
  output [31:0] PC
);

  wire [4:0] bit_extender_1_out;
  wire [31:0] shifter_1_out;

  Register #(.width(32)) register_1 (.D(NPC), .Q(PC), .clk(clk), .clr(reset));  // open: en
  Shifter #(.width(32), .shift("lr")) shifter_1 (.in(PC), .\dist (5'b00010), .out(shifter_1_out));
  Bit_Extender #(.in_width(32), .out_width(5)) bit_extender_1 (.in(shifter_1_out), .out(bit_extender_1_out));
  ROM #(.addrWidth(5), .dataWidth(32)) rom_1 (.addr(bit_extender_1_out), .data(out_4));  // open: sel
endmodule

module GRF (
  input  in_1,
  input  in_2,
  input  in_3,
  input  [4:0] in_4,
  input  [4:0] in_5,
  input  [4:0] in_6,
  input  [31:0] in_7,
  output [31:0] out_8,
  output [31:0] out_9
);

  wire [31:0] i0, i1, i2, i3, i4, i5, i6, i7, i8, i9, i10, i11, i12, i13, i14, i15, i16, i17, i18, i19, i20,
       i21, i22, i23, i24, i25, i26, i27, i28, i29, i30, i31, o1, o2, o3, o4, o5, o6, o7, o8, o9, o10, o11,
       o12, o13, o14, o15, o16, o17, o18, o19, o20, o21, o22, o23, o24, o25, o26, o27, o28, o29, o30, o31,
       register_1_q;

  Register #(.width(32)) register_1 (.D(i0), .en(in_3), .Q(register_1_q), .clk(in_1), .clr(in_2));
  Register #(.width(32)) register_2 (.D(i4), .en(in_3), .Q(o4), .clk(in_1), .clr(in_2));
  Register #(.width(32)) register_3 (.D(i8), .en(in_3), .Q(o8), .clk(in_1), .clr(in_2));
  Register #(.width(32)) register_4 (.D(i12), .en(in_3), .Q(o12), .clk(in_1), .clr(in_2));
  Register #(.width(32)) register_5 (.D(i16), .en(in_3), .Q(o16), .clk(in_1), .clr(in_2));
  Register #(.width(32)) register_6 (.D(i20), .en(in_3), .Q(o20), .clk(in_1), .clr(in_2));
  Register #(.width(32)) register_7 (.D(i24), .en(in_3), .Q(o24), .clk(in_1), .clr(in_2));
  Register #(.width(32)) register_8 (.D(i28), .en(in_3), .Q(o28), .clk(in_1), .clr(in_2));
  Demultiplexer #(.select(5), .width(32), .tristate("true")) demultiplexer_1 (
    .out0(i0), .out1(i1), .out2(i2), .out3(i3), .out4(i4), .out5(i5), .out6(i6), .out7(i7), .out8(i8),
    .out9(i9), .out10(i10), .out11(i11), .out12(i12), .out13(i13), .out14(i14), .out15(i15), .out16(i16),
    .out17(i17), .out18(i18), .out19(i19), .out20(i20), .out21(i21), .out22(i22), .out23(i23), .out24(i24),
    .out25(i25), .out26(i26), .out27(i27), .out28(i28), .out29(i29), .out30(i30), .out31(i31), .in(in_7),
    .sel(in_6));  // open: en
  Register #(.width(32)) register_9 (.D(i1), .en(in_3), .Q(o1), .clk(in_1), .clr(in_2));
  Register #(.width(32)) register_10 (.D(i5), .en(in_3), .Q(o5), .clk(in_1), .clr(in_2));
  Register #(.width(32)) register_11 (.D(i9), .en(in_3), .Q(o9), .clk(in_1), .clr(in_2));
  Register #(.width(32)) register_12 (.D(i13), .en(in_3), .Q(o13), .clk(in_1), .clr(in_2));
  Register #(.width(32)) register_13 (.D(i17), .en(in_3), .Q(o17), .clk(in_1), .clr(in_2));
  Register #(.width(32)) register_14 (.D(i21), .en(in_3), .Q(o21), .clk(in_1), .clr(in_2));
  Register #(.width(32)) register_15 (.D(i25), .en(in_3), .Q(o25), .clk(in_1), .clr(in_2));
  Register #(.width(32)) register_16 (.D(i29), .en(in_3), .Q(o29), .clk(in_1), .clr(in_2));
  Register #(.width(32)) register_17 (.D(i2), .en(in_3), .Q(o2), .clk(in_1), .clr(in_2));
  Register #(.width(32)) register_18 (.D(i6), .en(in_3), .Q(o6), .clk(in_1), .clr(in_2));
  Register #(.width(32)) register_19 (.D(i10), .en(in_3), .Q(o10), .clk(in_1), .clr(in_2));
  Register #(.width(32)) register_20 (.D(i14), .en(in_3), .Q(o14), .clk(in_1), .clr(in_2));
  Register #(.width(32)) register_21 (.D(i18), .en(in_3), .Q(o18), .clk(in_1), .clr(in_2));
  Register #(.width(32)) register_22 (.D(i22), .en(in_3), .Q(o22), .clk(in_1), .clr(in_2));
  Register #(.width(32)) register_23 (.D(i26), .en(in_3), .Q(o26), .clk(in_1), .clr(in_2));
  Register #(.width(32)) register_24 (.D(i30), .en(in_3), .Q(o30), .clk(in_1), .clr(in_2));
  Multiplexer #(.select(5), .width(32)) multiplexer_1 (
    .in0({32{1'b0}}), .in1(o1), .in2(o2), .in3(o3), .in4(o4), .in5(o5), .in6(o6), .in7(o7), .in8(o8),
    .in9(o9), .in10(o10), .in11(o11), .in12(o12), .in13(o13), .in14(o14), .in15(o15), .in16(o16), .in17(o17),
    .in18(o18), .in19(o19), .in20(o20), .in21(o21), .in22(o22), .in23(o23), .in24(o24), .in25(o25),
    .in26(o26), .in27(o27), .in28(o28), .in29(o29), .in30(o30), .in31(o31), .out(out_8), .sel(in_4));  // open: en
  Register #(.width(32)) register_25 (.D(i3), .en(in_3), .Q(o3), .clk(in_1), .clr(in_2));
  Register #(.width(32)) register_26 (.D(i7), .en(in_3), .Q(o7), .clk(in_1), .clr(in_2));
  Register #(.width(32)) register_27 (.D(i11), .en(in_3), .Q(o11), .clk(in_1), .clr(in_2));
  Register #(.width(32)) register_28 (.D(i15), .en(in_3), .Q(o15), .clk(in_1), .clr(in_2));
  Register #(.width(32)) register_29 (.D(i19), .en(in_3), .Q(o19), .clk(in_1), .clr(in_2));
  Register #(.width(32)) register_30 (.D(i23), .en(in_3), .Q(o23), .clk(in_1), .clr(in_2));
  Register #(.width(32)) register_31 (.D(i27), .en(in_3), .Q(o27), .clk(in_1), .clr(in_2));
  Register #(.width(32)) register_32 (.D(i31), .en(in_3), .Q(o31), .clk(in_1), .clr(in_2));
  Multiplexer #(.select(5), .width(32)) multiplexer_2 (
    .in0({32{1'b0}}), .in1(o1), .in2(o2), .in3(o3), .in4(o4), .in5(o5), .in6(o6), .in7(o7), .in8(o8),
    .in9(o9), .in10(o10), .in11(o11), .in12(o12), .in13(o13), .in14(o14), .in15(o15), .in16(o16), .in17(o17),
    .in18(o18), .in19(o19), .in20(o20), .in21(o21), .in22(o22), .in23(o23), .in24(o24), .in25(o25),
    .in26(o26), .in27(o27), .in28(o28), .in29(o29), .in30(o30), .in31(o31), .out(out_9), .sel(in_5));  // open: en

  // Other names for the same wires on the sheet: A1[4:0] = in_4; A2[4:0] = in_5; A3[4:0] = in_6; clk = in_1;
  //   RD1[31:0] = out_8; RD2[31:0] = out_9; reset = in_2; WD[31:0] = in_7; WE = in_3
endmodule

module ALU (
  input  [2:0] in_1,
  input  [31:0] in_2,
  input  [31:0] in_3,
  input  [4:0] in_4,
  output [31:0] ALUOut,
  output Zero
);

  wire [31:0] adder_1_out, and_1_out, or_1_out, subtractor_1_out;

  Adder #(.width(32)) adder_1 (.a(in_2), .b(in_3), .out(adder_1_out));  // open: cin, cout
  Subtractor #(.width(32)) subtractor_1 (.a(in_2), .b(in_3), .out(subtractor_1_out));  // open: bin, bout
  assign or_1_out = in_2 | in_3;  // OR_Gate or_1, 32 bits wide
  assign and_1_out = in_2 & in_3;  // AND_Gate and_1, 32 bits wide
  Multiplexer #(.select(3), .width(32)) multiplexer_1 (
    .in0(adder_1_out), .in1(subtractor_1_out), .in2(or_1_out), .in3(and_1_out), .out(ALUOut), .sel(in_1));  // open: in4, in5, in6, in7, en
  Comparator #(.width(32)) comparator_1 (.a({32{1'b0}}), .b(subtractor_1_out), .eq(Zero));  // open: gt, lt

  // Other names for the same wires on the sheet: ALUControl[2:0] = in_1; shamt[4:0] = in_4; SrcA[31:0] = in_2;
  //   SrcB[31:0] = in_3
endmodule

module Controller (
  input  [5:0] opcode,
  input  [5:0] funct,
  output [2:0] ALUControl,
  output MemRead,
  output MemWrite,
  output RegWrite,
  output [1:0] Mem2Reg,
  output EXTControl,
  output ALUSrc,
  output RegDst,
  output [1:0] NPCControl
);

  wire add, not_1_out, not_2_out, not_3_out, not_4_out, not_5_out, not_6_out, not_7_out, not_8_out,
       not_9_out, not_10_out, not_11_out, not_12_out, not_13_out, not_14_out, not_15_out, not_16_out,
       not_17_out, not_18_out, not_19_out, not_20_out, R, sub;

  not not_1 (not_1_out, opcode[0]);
  not not_2 (not_2_out, opcode[1]);
  not not_3 (not_3_out, opcode[2]);
  not not_4 (not_4_out, opcode[3]);
  not not_5 (not_5_out, opcode[4]);
  not not_6 (not_6_out, opcode[5]);
  not not_7 (not_7_out, funct[0]);
  not not_8 (not_8_out, funct[1]);
  not not_9 (not_9_out, funct[2]);
  not not_10 (not_10_out, funct[3]);
  not not_11 (not_11_out, funct[4]);
  not not_12 (not_12_out, funct[5]);
  and and_1 (R, not_1_out, not_2_out, not_3_out, not_4_out, not_5_out, not_6_out);
  and and_2 (add, R, not_7_out, not_8_out, not_9_out, not_10_out, not_11_out, funct[5]);
  not not_13 (not_13_out, add);
  and and_3 (sub, R, not_7_out, funct[1], not_9_out, not_10_out, not_11_out, funct[5]);
  not not_14 (not_14_out, sub);
  and and_4 (ALUControl[1], opcode[0], not_2_out, opcode[2], opcode[3], not_5_out, not_6_out);
  not not_15 (not_15_out, ALUControl[1]);
  and and_5 (Mem2Reg[0], opcode[0], opcode[1], not_3_out, not_4_out, not_5_out, not_6_out);
  not not_16 (not_16_out, Mem2Reg[0]);
  and and_6 (MemWrite, opcode[0], opcode[1], not_3_out, opcode[3], not_5_out, opcode[5]);
  not not_17 (not_17_out, MemWrite);
  and and_7 (NPCControl[0], not_1_out, not_2_out, opcode[2], not_4_out, not_5_out, not_6_out);
  not not_18 (not_18_out, NPCControl[0]);
  and and_8 (Mem2Reg[1], opcode[0], opcode[1], opcode[2], opcode[3], not_5_out, not_6_out);
  not not_19 (not_19_out, Mem2Reg[1]);
  and and_9 (NPCControl[1], not_1_out, opcode[1], not_3_out, not_4_out, not_5_out, not_6_out);
  not not_20 (not_20_out, NPCControl[1]);
  or or_1 (ALUControl[0], sub, ALUControl[1]);
  or or_2 (RegWrite, add, sub, ALUControl[1], Mem2Reg[0], Mem2Reg[1]);
  or or_3 (EXTControl, Mem2Reg[0], MemWrite, NPCControl[0]);
  or or_4 (ALUSrc, ALUControl[1], Mem2Reg[0], MemWrite, NPCControl[1]);
  or or_5 (RegDst, add, sub);

  assign ALUControl[2] = 1'b0;
  assign MemRead = Mem2Reg[0];

  // Other names for the same wires on the sheet: ori = ALUControl[1]; lw = Mem2Reg[0]; lui = Mem2Reg[1];
  //   beq = NPCControl[0]; j = NPCControl[1]; sw = MemWrite
endmodule

module EXT (
  input  EXTControl,
  input  [15:0] in_2,
  output [31:0] out_3
);

  wire [31:0] bit_extender_1_out, bit_extender_2_out;

  assign bit_extender_1_out = {{16{1'b0}}, in_2};  // Bit_Extender bit_extender_1
  assign bit_extender_2_out = {{16{in_2[15]}}, in_2};  // Bit_Extender bit_extender_2
  Multiplexer #(.width(32)) multiplexer_1 (
    .in0(bit_extender_1_out), .in1(bit_extender_2_out), .out(out_3), .sel(EXTControl));  // open: en
endmodule

module DM (
  input  in_1,
  input  in_2,
  input  in_3,
  input  in_4,
  input  [4:0] A,
  input  [31:0] WD,
  output [31:0] out_7
);

  RAM #(.addrWidth(5), .dataWidth(32), .bus("separate")) ram_1 (
    .addr(A), .din(WD), .data(out_7), .str(in_3), .clk(in_1), .ld(in_4), .clr(in_2));  // open: sel

  // Other names for the same wires on the sheet: clk = in_1; MemRead = in_4; MemWrite = in_3; reset = in_2
endmodule

module Splitter (
  input  [31:0] Instr,
  output [5:0] opcode,
  output [4:0] rs,
  output [4:0] rt,
  output [4:0] rd,
  output [4:0] shamt,
  output [5:0] funct,
  output [15:0] Imm16,
  output [25:0] Imm26
);

  Bit_Extender #(.in_width(32)) bit_extender_1 (.in(Instr), .out(Imm16));
  Bit_Extender #(.in_width(32), .out_width(26)) bit_extender_2 (.in(Instr), .out(Imm26));

  assign funct = Instr[5:0];
  assign opcode = Instr[31:26];
  assign rd = Instr[15:11];
  assign rs = Instr[25:21];
  assign rt = Instr[20:16];
  assign shamt = Instr[10:6];
endmodule
